// Logisim project AssignmentNo2a.circ as structural Verilog: 1 circuit, main circuit main
module main (
  input  X,
  input  in_2,
  input  Y,
  input  in_4,
  input  X_2,
  input  in_6,
  input  Y_2,
  input  in_8,
  input  in_9,
  input  X_3,
  input  in_11,
  output out_12,
  output out_13,
  output Z,
  output out_15,
  output Y_3,
  output out_17
);

  or or_1 (out_12, X, Y);
  and and_1 (Z, X_2, Y_2);
  not not_1 (Y_3, X_3);
  nand nand_1 (out_13, in_2, in_4);
  nor nor_1 (out_15, in_6, in_8);
  xor xor_1 (out_17, in_9, in_11);

  // Notes on the sheet:
  //   OR
  //   AND
  //   NOT
  //   2 a.
  //   ASSIGNMENT NUMBER 2
  //   NAND
  //   NOR
  //   EX-OR
endmodule
