// Logisim project AssignmentNo2b.circ as structural Verilog: 1 circuit, main circuit main
module main (
  input  in_1,
  input  in_2,
  input  in_3,
  input  A,
  input  B,
  input  C,
  input  D,
  output out_8,
  output out_9
);

  wire and_1_out, and_2_out, and_3_out, and_4_out, not_1_out, not_2_out, or_2_out;

  not not_1 (not_1_out, in_1);
  and and_1 (and_1_out, not_1_out, in_2);
  and and_2 (and_2_out, in_2, in_3);
  or or_1 (out_8, and_1_out, and_2_out);
  or or_2 (or_2_out, B, C);
  not not_2 (not_2_out, A);
  and and_3 (and_3_out, A, or_2_out);
  and and_4 (and_4_out, not_2_out, B, C, D);
  or or_3 (out_9, and_3_out, and_4_out);

  // Notes on the sheet:
  //   i.
  //   A'B + BC
  //   ASSIGNMENT NUMBER 2
  //   ii.
  //   A(B + C) + A'BCD
endmodule
