// Logisim project AssignmentNo3.circ as structural Verilog: 1 circuit, main circuit main
module main (
  input  A,
  input  A_2,
  input  A_3,
  input  A_4,
  input  B,
  input  A_5,
  input  B_2,
  input  A_6,
  input  in_9,
  input  B_3,
  input  A_7,
  input  A_8,
  input  B_4,
  input  B_5,
  output A_prime,
  output A_prime_2,
  output A_B,
  output A_B_2,
  output A_B_3,
  output A_B_4,
  output out_21,
  output out_22
);

  wire nand_1_out, nand_2_out, nand_3_out, nand_4_out, nand_5_out, nand_8_out, nand_9_out, nor_1_out,
       nor_2_out, nor_3_out, nor_4_out, nor_5_out, nor_9_out, nor_10_out;

  nand nand_1 (nand_1_out, A_4, B);
  nand nand_2 (nand_2_out, A_5, A_5);
  nand nand_3 (nand_3_out, B_3, B_3);
  nand nand_4 (nand_4_out, A_8, A_8);
  nand nand_5 (nand_5_out, B_4, B_4);
  nand nand_6 (A_prime, A, A);
  nand nand_7 (A_B, nand_1_out, nand_1_out);
  nand nand_8 (nand_8_out, nand_4_out, B_4);
  nand nand_9 (nand_9_out, A_8, nand_5_out);
  nand nand_10 (A_B_3, nand_2_out, nand_3_out);
  nand nand_11 (out_22, nand_8_out, nand_9_out);
  nor nor_1 (nor_1_out, A_6, in_9);
  nor nor_2 (nor_2_out, A_3, A_3);
  nor nor_3 (nor_3_out, B_2, B_2);
  nor nor_4 (nor_4_out, A_7, A_7);
  nor nor_5 (nor_5_out, B_5, B_5);
  nor nor_6 (A_prime_2, A_2, A_2);
  nor nor_7 (A_B_2, nor_2_out, nor_3_out);
  nor nor_8 (A_B_4, nor_1_out, nor_1_out);
  nor nor_9 (nor_9_out, nor_4_out, nor_5_out);
  nor nor_10 (nor_10_out, A_7, B_5);
  nor nor_11 (out_21, nor_9_out, nor_10_out);

  // Notes on the sheet:
  //   B
  //   A
  //   NAND
  //   A'B + AB'
  //   A'
  //   B'
  //   (A'.B) = A + B'
  //   (A.B')' = A' + B
  //   DLCA Assignment No. 3
  //   (A + B').(A' + B') = A'B + B'A
  //   B
  //   NOR
  //   A'
  //   B'
  //   (A' + B')' = (AB)
  //   (A + B)' = (A'B')
  //   (A'B' + AB')' = 
  //   A'B + AB'
endmodule
