// Logisim project AssignmentNo4.circ as structural Verilog: 4 circuits, main circuit main
module main (
  input  A,
  input  B,
  input  A_2,
  input  C_in,
  input  B_2,
  output S___A_xor_B,
  output out_7,
  output out_8,
  output out_9
);

  wire and_2_out, and_3_out, and_4_out, xor_2_out;

  xor xor_1 (S___A_xor_B, A_2, B_2);
  and and_1 (out_8, A_2, B_2);
  and and_2 (and_2_out, A, B);
  and and_3 (and_3_out, B, C_in);
  and and_4 (and_4_out, C_in, A);
  xor xor_2 (xor_2_out, A, B);
  xor xor_3 (out_7, xor_2_out, C_in);
  or or_1 (out_9, and_2_out, and_3_out, and_4_out);

  // Notes on the sheet:
  //   S = A xor B
  //   Half - adder
  //   C = A . B
  //   C = A . B
  //   Assignment No. 4
  //   S = A xor B xor C-in
  //   Full - adder
  //   C = AB + AC-in + BC-in
  //   S = A xor B xor C-in
  //   C = AB + AC-in + BC-in
endmodule

module ripple_carry_adder (
  input  in_1,
  input  in_2,
  input  in_3,
  input  in_4,
  input  in_5,
  input  in_6,
  input  in_7,
  input  in_8,
  input  in_9,
  output out_10,
  output out_11,
  output out_12,
  output out_13,
  output out_14
);

  wire and_1_out, and_2_out, and_3_out, and_4_out, and_5_out, and_6_out, and_7_out, and_8_out, and_9_out,
       and_10_out, and_11_out, and_12_out, or_1_out, or_2_out, or_3_out, xor_1_out, xor_3_out, xor_5_out,
       xor_7_out;

  and and_1 (and_1_out, in_1, in_2);
  and and_2 (and_2_out, in_2, in_3);
  and and_3 (and_3_out, in_3, in_1);
  xor xor_1 (xor_1_out, in_1, in_2);
  or or_1 (or_1_out, and_1_out, and_2_out, and_3_out);
  xor xor_2 (out_10, xor_1_out, in_3);
  and and_4 (and_4_out, or_1_out, in_4);
  and and_5 (and_5_out, in_4, in_5);
  and and_6 (and_6_out, in_5, or_1_out);
  xor xor_3 (xor_3_out, or_1_out, in_4);
  xor xor_4 (out_11, xor_3_out, in_5);
  or or_2 (or_2_out, and_4_out, and_5_out, and_6_out);
  xor xor_5 (xor_5_out, or_2_out, in_6);
  and and_7 (and_7_out, or_2_out, in_6);
  and and_8 (and_8_out, in_6, in_7);
  and and_9 (and_9_out, in_7, or_2_out);
  xor xor_6 (out_12, xor_5_out, in_7);
  or or_3 (or_3_out, and_7_out, and_8_out, and_9_out);
  xor xor_7 (xor_7_out, or_3_out, in_8);
  and and_10 (and_10_out, or_3_out, in_8);
  and and_11 (and_11_out, in_8, in_9);
  and and_12 (and_12_out, in_9, or_3_out);
  xor xor_8 (out_13, xor_7_out, in_9);
  or or_4 (out_14, and_10_out, and_11_out, and_12_out);
endmodule

module full_adder (
  input  in_1,
  input  in_2,
  input  in_3,
  output out_4,
  output out_5
);

  wire and_1_out, and_2_out, and_3_out, xor_1_out;

  xor xor_1 (xor_1_out, in_1, in_2);
  and and_1 (and_1_out, in_1, in_2);
  and and_2 (and_2_out, in_2, in_3);
  and and_3 (and_3_out, in_3, in_1);
  xor xor_2 (out_4, xor_1_out, in_3);
  or or_1 (out_5, and_1_out, and_2_out, and_3_out);
endmodule

module ripple_carry_adder___final (
  input  X0,
  input  Y0,
  input  C0,
  input  X1,
  input  Y1,
  input  X2,
  input  Y2,
  input  X3,
  input  Y3,
  output S0,
  output S1,
  output S2,
  output S3,
  output C4
);

  wire full_adder_1_out_5, full_adder_2_out_5, full_adder_3_out_5;

  full_adder full_adder_1 (.in_1(X0), .in_2(Y0), .in_3(C0), .out_4(S0), .out_5(full_adder_1_out_5));
  full_adder full_adder_2 (.in_1(full_adder_1_out_5), .in_2(X1), .in_3(Y1), .out_4(S1), .out_5(full_adder_2_out_5));
  full_adder full_adder_3 (.in_1(full_adder_2_out_5), .in_2(X2), .in_3(Y2), .out_4(S2), .out_5(full_adder_3_out_5));
  full_adder full_adder_4 (.in_1(full_adder_3_out_5), .in_2(X3), .in_3(Y3), .out_4(S3), .out_5(C4));

  // Notes on the sheet:
  //   C1
  //   Ripple Carry Adder
  //   C2
  //   C3
endmodule
