// Logisim project AssignmentNo5.circ as structural Verilog: 1 circuit, main circuit main
module main (
  input  G4,
  input  B4,
  input  G3,
  input  B3,
  input  G2,
  input  B2,
  input  G1,
  input  B1,
  output B4_2,
  output G4_2,
  output B3_2,
  output G3_2,
  output B2_2,
  output G2_2,
  output B1_2,
  output G1_2
);

  xor xor_1 (G3_2, B4, B3);
  xor xor_2 (G2_2, B3, B2);
  xor xor_3 (G1_2, B2, B1);
  xor xor_4 (B3_2, G4, G3);
  xor xor_5 (B2_2, B3_2, G2);
  xor xor_6 (B1_2, B2_2, G1);

  assign B4_2 = G4;
  assign G4_2 = B4;

  // Notes on the sheet:
  //   Binary to Gray
  //   ASSIGNMENT NO. 5
  //   Gray to Binary
endmodule
